# Fritzing sketch arduino-socketio (saved by Fritzing 0.8.7b)
breadboards: 1

parts:
  Componente1 = Arduino Uno (Rev3)
  S1 = Pushbutton [package="[THT]"]
  S2 = Pushbutton [package="[THT]"]
  R1 = Resistor [tolerance=±5% resistance=10k package=THT]
  R2 = Resistor [tolerance=±5% resistance=10k package=THT]

nets:
  N1: Componente1.D6_PWM, S2.Pin_3, S2.Pin_4, R2.Pin_1
  N2: Componente1.D7, S1.Pin_3, S1.Pin_4, R1.Pin_1
  N3: Componente1.5V, S1.Pin_1, S1.Pin_2, S2.Pin_1, S2.Pin_2
  N4: Componente1.GND, R1.Pin_0, R2.Pin_0
