# Fritzing sketch arduino-firmata (saved by Fritzing 0.8.7b)
breadboards: 1

parts:
  Componente1 = Arduino Uno (Rev3)
  LED1 = LED - 5mm [color="Green (555nm)" package="5 mm [THT]"]
  R1 = Resistor [tolerance=±5% resistance=220 package=THT]

nets:
  N1: Componente1.D13/SCK, LED1.anode
  N2: Componente1.GND, R1.Pin_1
  N3: LED1.cathode, R1.Pin_0
